// Logisim project ChangeIn10_Sincrono.circ as structural Verilog: 2 circuits, main circuit main
module main (
  input  CLK,
  input  Clear,
  output Changed
);

  wire and_1_out, and_2_out, controler_1_j1, controler_1_j2, controler_1_j3, controler_1_k1, controler_1_k2,
       controler_1_k3, not_1_out, not_2_out, not_3_out, not_4_out, or_1_out;
  wire [3:0] Q0_q;

  Hex_Digit_Display hex_digit_display_1 (.value(Q0_q));  // open: dp
  and and_1 (and_1_out, Q0_q[3], not_1_out, Q0_q[1], not_3_out);
  or or_1 (or_1_out, Clear, and_1_out);
  J_K_Flip_Flop #(.trigger("falling")) Q3 (
    .J(controler_1_j3), .clk(CLK), .K(controler_1_k3), .Q(Q0_q[3]), .reset(or_1_out));  // open: Qn, preset, en
  not not_1 (not_1_out, Q0_q[2]);
  not not_2 (not_2_out, Q0_q[2]);
  J_K_Flip_Flop #(.trigger("falling")) Q2 (
    .J(controler_1_j2), .clk(CLK), .K(controler_1_k2), .Q(Q0_q[2]), .reset(or_1_out));  // open: Qn, preset, en
  J_K_Flip_Flop #(.trigger("falling")) Q1 (
    .J(controler_1_j1), .clk(CLK), .K(controler_1_k1), .Q(Q0_q[1]), .reset(or_1_out));  // open: Qn, preset, en
  not not_3 (not_3_out, Q0_q[0]);
  not not_4 (not_4_out, Q0_q[1]);
  T_Flip_Flop #(.trigger("falling")) Q0 (.clk(CLK), .T(1'b1), .Q(Q0_q[0]), .reset(or_1_out));  // open: Qn, preset, en
  controler controler_1 (
    .J3(controler_1_j3), .K3(controler_1_k3), .J2(controler_1_j2), .K2(controler_1_k2), .J1(controler_1_j1),
    .K1(controler_1_k1), .Q2(Q0_q[2]), .Q1(Q0_q[1]), .Q0(Q0_q[0]));
  and and_2 (and_2_out, Q0_q[3], not_2_out, not_4_out, Q0_q[0]);
  T_Flip_Flop t_ff_1 (.clk(CLK), .T(and_2_out), .Q(Changed), .reset(Clear));  // open: Qn, preset, en
endmodule

module controler (
  input  Q2,
  input  Q1,
  input  Q0,
  output J3,
  output K3,
  output J2,
  output K2,
  output J1,
  output K1
);

  and and_1 (J3, Q1, Q2, Q0);
  and and_2 (J2, Q0, Q1);

  assign J1 = Q0;
  assign K1 = Q0;
  assign K2 = J2;
  assign K3 = 1'b0;
endmodule
