// Logisim project Clock.circ as structural Verilog: 6 circuits, main circuit main
module main (
);

  wire button_1_out, button_2_out, button_3_out, button_4_out, button_5_out, button_6_out, button_7_out,
       button_8_out, button_9_out, button_10_out;
  wire [3:0] n24hclock_1_hoursd, n24hclock_1_hoursu, n24hclock_1_minutesd, n24hclock_1_minutesu,
       n24hclock_1_secondsd, n24hclock_1_secondsu;

  Hex_Digit_Display hex_digit_display_1 (.value(n24hclock_1_hoursd));  // open: dp
  _24hClock u_24hclock_1 (
    .ResetAll(button_1_out), .SetDHours(button_2_out), .SetUHours(button_3_out), .ResetHours(button_4_out),
    .SetDMinutes(button_5_out), .SetUMinutes(button_6_out), .ResetMinutes(button_7_out),
    .SetDSeconds(button_8_out), .SetUSeconds(button_9_out), .ResetSeconds(button_10_out),
    .HoursD(n24hclock_1_hoursd), .HoursU(n24hclock_1_hoursu), .MinutesD(n24hclock_1_minutesd),
    .MinutesU(n24hclock_1_minutesu), .SecondsD(n24hclock_1_secondsd), .SecondsU(n24hclock_1_secondsu));
  Hex_Digit_Display hex_digit_display_2 (.value(n24hclock_1_hoursu));  // open: dp
  Hex_Digit_Display hex_digit_display_3 (.value(n24hclock_1_minutesd));  // open: dp
  Hex_Digit_Display hex_digit_display_4 (.value(n24hclock_1_minutesu));  // open: dp
  Hex_Digit_Display hex_digit_display_5 (.value(n24hclock_1_secondsu));  // open: dp
  Hex_Digit_Display hex_digit_display_6 (.value(n24hclock_1_secondsd));  // open: dp
  Button button_1 (.out(button_1_out));
  Button button_2 (.out(button_2_out));
  Button button_3 (.out(button_3_out));
  Button button_4 (.out(button_4_out));
  Button button_5 (.out(button_5_out));
  Button button_6 (.out(button_6_out));
  Button button_7 (.out(button_7_out));
  Button button_8 (.out(button_8_out));
  Button button_9 (.out(button_9_out));
  Button button_10 (.out(button_10_out));
endmodule

module CountTo9 (
  input  Clock,
  input  Reset,
  output [3:0] A3___A0,
  output Set
);

  wire or_1_out, or_2_out, or_3_out, or_4_out;

  and and_1 (Set, A3___A0[3], ~A3___A0[2], A3___A0[1], ~A3___A0[0]);  // AND_Gate
  J_K_Flip_Flop #(.trigger("falling")) j_k_ff_1 (
    .J(1'b1), .clk(Clock), .K(1'b1), .Q(A3___A0[0]), .reset(or_2_out));  // open: Qn, preset, en
  or or_1 (or_1_out, Reset, Set);
  or or_2 (or_2_out, Reset, Set);
  J_K_Flip_Flop #(.trigger("falling")) j_k_ff_2 (
    .J(1'b1), .clk(A3___A0[1]), .K(1'b1), .Q(A3___A0[2]), .reset(or_3_out));  // open: Qn, preset, en
  J_K_Flip_Flop #(.trigger("falling")) j_k_ff_3 (
    .J(1'b1), .clk(A3___A0[0]), .K(1'b1), .Q(A3___A0[1]), .reset(or_1_out));  // open: Qn, preset, en
  or or_3 (or_3_out, Reset, Set);
  J_K_Flip_Flop #(.trigger("falling")) j_k_ff_4 (
    .J(1'b1), .clk(A3___A0[2]), .K(1'b1), .Q(A3___A0[3]), .reset(or_4_out));  // open: Qn, preset, en
  or or_4 (or_4_out, Reset, Set);
endmodule

module CountTo5 (
  input  Clock,
  input  Reset,
  output [3:0] A3___A0,
  output Set
);

  wire or_1_out, or_2_out, or_3_out, or_4_out;

  and and_1 (Set, ~A3___A0[3], A3___A0[2], A3___A0[1], ~A3___A0[0]);  // AND_Gate
  J_K_Flip_Flop #(.trigger("falling")) j_k_ff_1 (
    .J(1'b1), .clk(Clock), .K(1'b1), .Q(A3___A0[0]), .reset(or_2_out));  // open: Qn, preset, en
  or or_1 (or_1_out, Reset, Set);
  or or_2 (or_2_out, Reset, Set);
  J_K_Flip_Flop #(.trigger("falling")) j_k_ff_2 (
    .J(1'b1), .clk(A3___A0[1]), .K(1'b1), .Q(A3___A0[2]), .reset(or_3_out));  // open: Qn, preset, en
  J_K_Flip_Flop #(.trigger("falling")) j_k_ff_3 (
    .J(1'b1), .clk(A3___A0[0]), .K(1'b1), .Q(A3___A0[1]), .reset(or_1_out));  // open: Qn, preset, en
  or or_3 (or_3_out, Reset, Set);
  J_K_Flip_Flop #(.trigger("falling")) j_k_ff_4 (
    .J(1'b1), .clk(A3___A0[2]), .K(1'b1), .Q(A3___A0[3]), .reset(or_4_out));  // open: Qn, preset, en
  or or_4 (or_4_out, Reset, Set);
endmodule

module IsIn2CountTo9 (
  input  Clock,
  input  Reset,
  output [3:0] A3___A0,
  output IsIn2,
  output SetIn9
);

  wire or_1_out, or_2_out, or_3_out, or_4_out;

  and and_1 (IsIn2, ~A3___A0[3], ~A3___A0[2], A3___A0[1], ~A3___A0[0]);  // AND_Gate
  and and_2 (SetIn9, A3___A0[3], ~A3___A0[2], A3___A0[1], ~A3___A0[0]);  // AND_Gate
  J_K_Flip_Flop #(.trigger("falling")) j_k_ff_1 (
    .J(1'b1), .clk(Clock), .K(1'b1), .Q(A3___A0[0]), .reset(or_2_out));  // open: Qn, preset, en
  or or_1 (or_1_out, Reset, SetIn9);
  or or_2 (or_2_out, Reset, SetIn9);
  J_K_Flip_Flop #(.trigger("falling")) j_k_ff_2 (
    .J(1'b1), .clk(A3___A0[0]), .K(1'b1), .Q(A3___A0[1]), .reset(or_1_out));  // open: Qn, preset, en
  J_K_Flip_Flop #(.trigger("falling")) j_k_ff_3 (
    .J(1'b1), .clk(A3___A0[1]), .K(1'b1), .Q(A3___A0[2]), .reset(or_3_out));  // open: Qn, preset, en
  or or_3 (or_3_out, Reset, SetIn9);
  J_K_Flip_Flop #(.trigger("falling")) j_k_ff_4 (
    .J(1'b1), .clk(A3___A0[2]), .K(1'b1), .Q(A3___A0[3]), .reset(or_4_out));  // open: Qn, preset, en
  or or_4 (or_4_out, Reset, SetIn9);
endmodule

module CountTo3_9 (
  input  Clock,
  input  Reset,
  output [3:0] A3___A0,
  output SetIn3,
  output SetIn9
);

  wire or_1_out, or_2_out, or_3_out, or_4_out;

  and and_1 (SetIn3, ~A3___A0[3], A3___A0[2], ~A3___A0[1], ~A3___A0[0]);  // AND_Gate
  and and_2 (SetIn9, A3___A0[3], ~A3___A0[2], A3___A0[1], ~A3___A0[0]);  // AND_Gate
  J_K_Flip_Flop #(.trigger("falling")) j_k_ff_1 (
    .J(1'b1), .clk(Clock), .K(1'b1), .Q(A3___A0[0]), .reset(or_2_out));  // open: Qn, preset, en
  or or_1 (or_1_out, Reset, SetIn9);
  or or_2 (or_2_out, Reset, SetIn9);
  J_K_Flip_Flop #(.trigger("falling")) j_k_ff_2 (
    .J(1'b1), .clk(A3___A0[0]), .K(1'b1), .Q(A3___A0[1]), .reset(or_1_out));  // open: Qn, preset, en
  J_K_Flip_Flop #(.trigger("falling")) j_k_ff_3 (
    .J(1'b1), .clk(A3___A0[1]), .K(1'b1), .Q(A3___A0[2]), .reset(or_3_out));  // open: Qn, preset, en
  or or_3 (or_3_out, Reset, SetIn9);
  J_K_Flip_Flop #(.trigger("falling")) j_k_ff_4 (
    .J(1'b1), .clk(A3___A0[2]), .K(1'b1), .Q(A3___A0[3]), .reset(or_4_out));  // open: Qn, preset, en
  or or_4 (or_4_out, Reset, SetIn9);
endmodule

module _24hClock (
  input  ResetAll,
  input  SetDHours,
  input  SetUHours,
  input  ResetHours,
  input  SetDMinutes,
  input  SetUMinutes,
  input  ResetMinutes,
  input  SetDSeconds,
  input  SetUSeconds,
  input  ResetSeconds,
  output [3:0] HoursD,
  output [3:0] HoursU,
  output [3:0] MinutesD,
  output [3:0] MinutesU,
  output [3:0] SecondsD,
  output [3:0] SecondsU
);

  wire and_1_out, clock_1_out, countto3_9_1_setin3, countto3_9_1_setin9, countto5_1_set, countto5_2_set,
       countto9_1_set, countto9_2_set, isin2countto9_1_isin2, or_1_out, or_2_out, or_3_out, or_4_out,
       or_5_out, or_6_out, or_7_out, or_8_out, or_9_out, or_10_out;

  and and_1 (and_1_out, isin2countto9_1_isin2, countto3_9_1_setin3);
  IsIn2CountTo9 isin2countto9_1 (
    .A3___A0(HoursD), .Clock(or_1_out), .Reset(or_6_out), .IsIn2(isin2countto9_1_isin2));  // open: SetIn9
  or or_1 (or_1_out, countto3_9_1_setin9, SetDHours);
  CountTo3_9 countto3_9_1 (
    .A3___A0(HoursU), .SetIn3(countto3_9_1_setin3), .Clock(or_2_out), .Reset(or_7_out),
    .SetIn9(countto3_9_1_setin9));
  or or_2 (or_2_out, countto5_1_set, SetUHours);
  CountTo5 countto5_1 (.A3___A0(MinutesD), .Clock(or_3_out), .Reset(or_8_out), .Set(countto5_1_set));
  or or_3 (or_3_out, countto9_1_set, SetDMinutes);
  CountTo9 countto9_1 (.A3___A0(MinutesU), .Set(countto9_1_set), .Clock(or_4_out), .Reset(or_8_out));
  or or_4 (or_4_out, countto5_2_set, SetUMinutes);
  CountTo5 countto5_2 (.A3___A0(SecondsD), .Clock(or_5_out), .Reset(or_9_out), .Set(countto5_2_set));
  or or_5 (or_5_out, SetDSeconds, countto9_2_set);
  CountTo9 countto9_2 (.A3___A0(SecondsU), .Set(countto9_2_set), .Clock(or_10_out), .Reset(or_9_out));
  or or_6 (or_6_out, ResetHours, ResetAll, and_1_out);
  or or_7 (or_7_out, and_1_out, ResetAll, ResetHours);
  or or_8 (or_8_out, ResetMinutes, ResetAll);
  or or_9 (or_9_out, ResetAll, ResetSeconds);
  or or_10 (or_10_out, SetUSeconds, clock_1_out);
  Clock clock_1 (.out(clock_1_out));
endmodule
