// Logisim project Flip-Flop_SR.circ as structural Verilog
module SR_Flip_Flop (
  input  S,
  input  R,
  output Q,
  output Q_prime
);

  wire not_1_out, not_2_out;

  not not_1 (not_1_out, S);
  not not_2 (not_2_out, R);
  nand nand_1 (Q, not_1_out, Q_prime);
  nand nand_2 (Q_prime, Q, not_2_out);

  // Notes on the sheet:
  //   SR_Flip-Flop
endmodule

module JK_Flip_Flop (
  input  J,
  input  clock,
  input  K
);

  wire nand_1_out, nand_2_out, sr_ff_1_q, sr_ff_1_q_prime;

  nand nand_1 (nand_1_out, sr_ff_1_q_prime, J, clock);
  nand nand_2 (nand_2_out, clock, K, sr_ff_1_q);
  SR_Flip_Flop sr_ff_1 (.S(nand_1_out), .R(nand_2_out), .Q(sr_ff_1_q), .Q_prime(sr_ff_1_q_prime));
endmodule
