// Logisim project Sequencia_Sicrona.circ as structural Verilog: 7 circuits, main circuit Trabalho
module Trabalho (
);

  wire and_1_out, and_2_out, and_3_out, and_4_out, and_5_out, and_6_out, and_7_out, and_8_out, and_9_out,
       and_10_out, changein10_1_changed, clock_1_out, j0_k0_1_j0, j0_k0_1_k0, j1_k1_1_j1, j1_k1_1_k1,
       j2_k2_1_j2, j2_k2_1_k2, j3_k3_1_j3, j3_k3_1_k3, or_1_out, or_2_out, or_3_out, or_4_out, or_5_out,
       Q0_2_qn, Q0_qn, Q1_2_qn, Q1_qn, Q2_2_qn, Q2_qn, Q3_2_qn, Q3_qn, Reset_out;
  wire [3:0] multiplexer_1_out, Q0_2_q, Q0_q;

  Hex_Digit_Display hex_digit_display_1 (.value(multiplexer_1_out));  // open: dp
  Multiplexer #(.width(4), .enable("false")) multiplexer_1 (
    .in0(Q0_2_q), .in1(Q0_q), .out(multiplexer_1_out), .sel(changein10_1_changed));
  and and_1 (and_1_out, Q0_2_q[0], Q0_2_q[1], Q0_2_q[2], Q0_2_q[3]);
  and and_2 (and_2_out, Q0_q[0], ~Q0_q[1], Q0_q[2], ~Q0_q[3]);  // AND_Gate
  Clock clock_1 (.out(clock_1_out));
  and and_3 (and_3_out, clock_1_out, and_2_out);
  and and_4 (and_4_out, and_1_out, clock_1_out);
  Hex_Digit_Display hex_digit_display_2 (.value(Q0_2_q));  // open: dp
  ChangeIn10 changein10_1 (.CLK(clock_1_out), .Clear(Reset_out), .Changed(changein10_1_changed));
  Hex_Digit_Display hex_digit_display_3 (.value(Q0_q));  // open: dp
  Button Reset (.out(Reset_out));
  or or_1 (or_1_out, and_6_out, and_5_out);
  and and_5 (and_5_out, Q0_q[3], Q0_q[1]);
  and and_6 (and_6_out, Q3_2_qn, Q2_2_qn);
  J_K_Flip_Flop Q3 (
    .J(j3_k3_1_j3), .clk(and_3_out), .K(j3_k3_1_k3), .Q(Q0_2_q[3]), .Qn(Q3_qn), .reset(Reset_out));  // open: preset, en
  J3___K3 j3_k3_1 (
    .J3(j3_k3_1_j3), .K3(j3_k3_1_k3), .Q2(Q0_2_q[2]), .Q2_prime(Q2_qn), .Q1(Q0_2_q[1]), .Q1_prime(Q1_2_qn),
    .Q0(Q0_2_q[0]), .Q0_prime(Q0_2_qn));
  J_K_Flip_Flop Q0 (
    .J(Q0_q[1]), .clk(and_4_out), .K(or_1_out), .Q(Q0_q[0]), .Qn(Q0_qn), .preset(Reset_out));  // open: en, reset
  J_K_Flip_Flop Q2 (
    .J(j2_k2_1_j2), .clk(and_3_out), .K(j2_k2_1_k2), .Q(Q0_2_q[2]), .Qn(Q2_qn), .reset(Reset_out));  // open: preset, en
  J2___K2 j2_k2_1 (
    .J2(j2_k2_1_j2), .K2(j2_k2_1_k2), .Q3(Q0_2_q[3]), .Q3_prime(Q3_qn), .Q1(Q0_2_q[1]), .Q1_prime(Q1_2_qn),
    .Q0(Q0_2_q[0]), .Q0_prime(Q0_2_qn));
  J_K_Flip_Flop Q1 (
    .J(1'b1), .clk(and_4_out), .K(or_2_out), .Q(Q0_q[1]), .Qn(Q1_qn), .reset(Reset_out));  // open: preset, en
  or or_2 (or_2_out, Q0_q[2], and_7_out);
  and and_7 (and_7_out, Q0_q[0], Q3_2_qn);
  J_K_Flip_Flop Q1_2 (
    .J(j1_k1_1_j1), .clk(and_3_out), .K(j1_k1_1_k1), .Q(Q0_2_q[1]), .Qn(Q1_2_qn), .preset(Reset_out));  // open: en, reset
  J1___K1 j1_k1_1 (
    .J1(j1_k1_1_j1), .K1(j1_k1_1_k1), .Q3(Q0_2_q[3]), .Q3_prime(Q3_qn), .Q2(Q0_2_q[2]), .Q2_prime(Q2_qn),
    .Q0(Q0_2_q[0]), .Q0_prime(Q0_2_qn));
  and and_8 (and_8_out, Q0_q[0], Q0_q[1]);
  or or_3 (or_3_out, Q0_q[3], and_8_out);
  or or_4 (or_4_out, Q0_q[3], Q0_q[0]);
  J_K_Flip_Flop Q0_2 (
    .J(j0_k0_1_j0), .clk(and_3_out), .K(j0_k0_1_k0), .Q(Q0_2_q[0]), .Qn(Q0_2_qn), .reset(Reset_out));  // open: preset, en
  J0___K0 j0_k0_1 (
    .J0(j0_k0_1_j0), .K0(j0_k0_1_k0), .Q3(Q0_2_q[3]), .Q3_prime(Q3_qn), .Q2(Q0_2_q[2]), .Q2_prime(Q2_qn),
    .Q1(Q0_2_q[1]), .Q1_prime(Q1_2_qn));
  J_K_Flip_Flop Q2_2 (
    .J(or_3_out), .clk(and_4_out), .K(or_4_out), .Q(Q0_q[2]), .Qn(Q2_2_qn), .preset(Reset_out));  // open: en, reset
  and and_9 (and_9_out, Q0_qn, Q1_qn);
  and and_10 (and_10_out, Q2_2_qn, Q0_qn);
  or or_5 (or_5_out, and_9_out, and_10_out);
  J_K_Flip_Flop Q3_2 (
    .J(or_5_out), .clk(and_4_out), .K(Q0_q[0]), .Q(Q0_q[3]), .Qn(Q3_2_qn), .reset(Reset_out));  // open: preset, en

  // Notes on the sheet:
  //   Diogo Morgado Viana. Sequência: 2... 10... 3... 4... 1... 11... 8... 5... 12... 15...
  //   Gabriel Schaldach Morgado. Sequência: 5... 3... 4... 14... 9... 7... 1... 2... 11... 6...
  //   Q3
  //   Q2
  //   Q1
  //   Q0
endmodule

module J3___K3 (
  input  Q2,
  input  Q2_prime,
  input  Q1,
  input  Q1_prime,
  input  Q0,
  input  Q0_prime,
  output J3,
  output K3
);

  wire and_1_out, and_2_out;

  or or_1 (K3, and_1_out, and_2_out);
  xor xor_1 (J3, Q1, Q0);
  and and_1 (and_1_out, Q2_prime, Q0_prime);
  and and_2 (and_2_out, Q2, Q0);
endmodule

module J2___K2 (
  input  Q3,
  input  Q3_prime,
  input  Q1,
  input  Q1_prime,
  input  Q0,
  input  Q0_prime,
  output J2,
  output K2
);

  wire and_1_out, and_2_out, and_3_out;

  or or_1 (J2, and_2_out, and_3_out);
  or or_2 (K2, Q1, and_1_out);
  and and_1 (and_1_out, Q3_prime, Q0_prime);
  and and_2 (and_2_out, Q3, Q1_prime);
  and and_3 (and_3_out, Q3_prime, Q1, Q0);
endmodule

module J1___K1 (
  input  Q3,
  input  Q3_prime,
  input  Q2,
  input  Q2_prime,
  input  Q0,
  input  Q0_prime,
  output J1,
  output K1
);

  wire and_2_out, and_3_out;

  or or_1 (J1, and_2_out, and_3_out);
  and and_1 (K1, Q0, Q2_prime);
  and and_2 (and_2_out, Q3, Q2);
  and and_3 (and_3_out, Q3_prime, Q2_prime);
endmodule

module J0___K0 (
  input  Q3,
  input  Q3_prime,
  input  Q2,
  input  Q2_prime,
  input  Q1,
  input  Q1_prime,
  output J0,
  output K0
);

  or or_1 (J0, Q3, Q1_prime);
  or or_2 (K0, Q1, Q2);
endmodule

module \Sequência_Sincrona  (
);

  wire clock_1_out, j0_k0_1_j0, j0_k0_1_k0, j1_k1_1_j1, j1_k1_1_k1, j2_k2_1_j2, j2_k2_1_k2, j3_k3_1_j3,
       j3_k3_1_k3, Q0_qn, Q1_qn, Q2_qn, Q3_qn;
  wire [3:0] Q0_q;

  Hex_Digit_Display hex_digit_display_1 (.value(Q0_q));  // open: dp
  Clock clock_1 (.out(clock_1_out));
  J_K_Flip_Flop Q3 (
    .J(j3_k3_1_j3), .clk(clock_1_out), .K(j3_k3_1_k3), .Q(Q0_q[3]), .Qn(Q3_qn));  // open: preset, en, reset
  J3___K3 j3_k3_1 (
    .J3(j3_k3_1_j3), .K3(j3_k3_1_k3), .Q2(Q0_q[2]), .Q2_prime(Q2_qn), .Q1(Q0_q[1]), .Q1_prime(Q1_qn),
    .Q0(Q0_q[0]), .Q0_prime(Q0_qn));
  J_K_Flip_Flop Q2 (
    .J(j2_k2_1_j2), .clk(clock_1_out), .K(j2_k2_1_k2), .Q(Q0_q[2]), .Qn(Q2_qn));  // open: preset, en, reset
  J2___K2 j2_k2_1 (
    .J2(j2_k2_1_j2), .K2(j2_k2_1_k2), .Q3(Q0_q[3]), .Q3_prime(Q3_qn), .Q1(Q0_q[1]), .Q1_prime(Q1_qn),
    .Q0(Q0_q[0]), .Q0_prime(Q0_qn));
  J_K_Flip_Flop Q1 (
    .J(j1_k1_1_j1), .clk(clock_1_out), .K(j1_k1_1_k1), .Q(Q0_q[1]), .Qn(Q1_qn));  // open: preset, en, reset
  J1___K1 j1_k1_1 (
    .J1(j1_k1_1_j1), .K1(j1_k1_1_k1), .Q3(Q0_q[3]), .Q3_prime(Q3_qn), .Q2(Q0_q[2]), .Q2_prime(Q2_qn),
    .Q0(Q0_q[0]), .Q0_prime(Q0_qn));
  J_K_Flip_Flop Q0 (
    .J(j0_k0_1_j0), .clk(clock_1_out), .K(j0_k0_1_k0), .Q(Q0_q[0]), .Qn(Q0_qn));  // open: preset, en, reset
  J0___K0 j0_k0_1 (
    .J0(j0_k0_1_j0), .K0(j0_k0_1_k0), .Q3(Q0_q[3]), .Q3_prime(Q3_qn), .Q2(Q0_q[2]), .Q2_prime(Q2_qn),
    .Q1(Q0_q[1]), .Q1_prime(Q1_qn));

  // Notes on the sheet:
  //   Q3
  //   Q2
  //   Q1
  //   Q0
endmodule

module ChangeIn10 (
  input  CLK,
  input  Clear,
  output Changed
);

  wire and_1_out, and_2_out, or_1_out, t_ff_1_q, t_ff_1_qn, t_ff_2_q, t_ff_3_q, t_ff_3_qn, t_ff_4_q;

  and and_1 (and_1_out, t_ff_1_q, t_ff_2_q, t_ff_3_qn, t_ff_4_q);
  or or_1 (or_1_out, Clear, and_1_out);
  T_Flip_Flop #(.trigger("falling")) t_ff_1 (
    .clk(CLK), .T(1'b1), .Q(t_ff_1_q), .Qn(t_ff_1_qn), .reset(or_1_out));  // open: preset, en
  T_Flip_Flop #(.trigger("falling")) t_ff_2 (
    .clk(t_ff_1_q), .T(1'b1), .Q(t_ff_2_q), .reset(or_1_out));  // open: Qn, preset, en
  T_Flip_Flop #(.trigger("falling")) t_ff_3 (
    .clk(t_ff_2_q), .T(1'b1), .Q(t_ff_3_q), .Qn(t_ff_3_qn), .reset(or_1_out));  // open: preset, en
  T_Flip_Flop #(.trigger("falling")) t_ff_4 (
    .clk(t_ff_3_q), .T(1'b1), .Q(t_ff_4_q), .reset(or_1_out));  // open: Qn, preset, en
  and and_2 (and_2_out, t_ff_1_qn, t_ff_2_q, t_ff_3_qn, t_ff_4_q);
  T_Flip_Flop t_ff_5 (.clk(CLK), .T(and_2_out), .Q(Changed), .reset(Clear));  // open: Qn, preset, en
endmodule
