// Logisim project ULA2.circ as structural Verilog: 13 circuits, main circuit main
module main (
  input  [3:0] in_1,
  input  [3:0] in_2,
  input  [2:0] S3___S0,
  output [3:0] out_4
);

  wire n4bit_negative_display_1_a, n4bit_negative_display_1_b, n4bit_negative_display_1_c,
       n4bit_negative_display_1_cout, n4bit_negative_display_1_d, n4bit_negative_display_1_e,
       n4bit_negative_display_1_f, n4bit_negative_display_1_g, n4bit_negative_display_2_a,
       n4bit_negative_display_2_b, n4bit_negative_display_2_c, n4bit_negative_display_2_cout,
       n4bit_negative_display_2_d, n4bit_negative_display_2_e, n4bit_negative_display_2_f,
       n4bit_negative_display_2_g, n4bit_negative_display_3_a, n4bit_negative_display_3_b,
       n4bit_negative_display_3_c, n4bit_negative_display_3_cout, n4bit_negative_display_3_d,
       n4bit_negative_display_3_e, n4bit_negative_display_3_f, n4bit_negative_display_3_g, ula_1_of, ula_1_zf;

  _4bit_Negative_Display u_4bit_negative_display_1 (
    .in_1(in_1), .a(n4bit_negative_display_1_a), .b(n4bit_negative_display_1_b),
    .c(n4bit_negative_display_1_c), .d(n4bit_negative_display_1_d), .e(n4bit_negative_display_1_e),
    .f(n4bit_negative_display_1_f), .g(n4bit_negative_display_1_g), .Cout(n4bit_negative_display_1_cout));
  _7_Segment_Display u_7_segment_display_1 (.g(n4bit_negative_display_1_cout));  // open: f, a, b, e, d, c, dp
  _4bit_Negative_Display u_4bit_negative_display_2 (
    .in_1(out_4), .a(n4bit_negative_display_2_a), .b(n4bit_negative_display_2_b),
    .c(n4bit_negative_display_2_c), .d(n4bit_negative_display_2_d), .e(n4bit_negative_display_2_e),
    .f(n4bit_negative_display_2_f), .g(n4bit_negative_display_2_g), .Cout(n4bit_negative_display_2_cout));
  _7_Segment_Display u_7_segment_display_2 (
    .g(n4bit_negative_display_1_g), .f(n4bit_negative_display_1_f), .a(n4bit_negative_display_1_a),
    .b(n4bit_negative_display_1_b), .e(n4bit_negative_display_1_e), .d(n4bit_negative_display_1_d),
    .c(n4bit_negative_display_1_c));  // open: dp
  _7_Segment_Display u_7_segment_display_3 (.g(n4bit_negative_display_2_cout));  // open: f, a, b, e, d, c, dp
  _4bit_Negative_Display u_4bit_negative_display_3 (
    .in_1(in_2), .a(n4bit_negative_display_3_a), .b(n4bit_negative_display_3_b),
    .c(n4bit_negative_display_3_c), .d(n4bit_negative_display_3_d), .e(n4bit_negative_display_3_e),
    .f(n4bit_negative_display_3_f), .g(n4bit_negative_display_3_g), .Cout(n4bit_negative_display_3_cout));
  LED OF (.in(ula_1_of));
  ULA ula_1 (.S2___S0(S3___S0), .OF(ula_1_of), .ZF(ula_1_zf), .A3___A0(in_1), .B3___B0(in_2), .Y3___Y0(out_4));
  LED ZF (.in(ula_1_zf));
  _7_Segment_Display u_7_segment_display_4 (
    .g(n4bit_negative_display_2_g), .f(n4bit_negative_display_2_f), .a(n4bit_negative_display_2_a),
    .b(n4bit_negative_display_2_b), .e(n4bit_negative_display_2_e), .d(n4bit_negative_display_2_d),
    .c(n4bit_negative_display_2_c));  // open: dp
  _7_Segment_Display u_7_segment_display_5 (
    .g(n4bit_negative_display_3_g), .f(n4bit_negative_display_3_f), .a(n4bit_negative_display_3_a),
    .b(n4bit_negative_display_3_b), .e(n4bit_negative_display_3_e), .d(n4bit_negative_display_3_d),
    .c(n4bit_negative_display_3_c));  // open: dp
  _7_Segment_Display u_7_segment_display_6 (.g(n4bit_negative_display_3_cout));  // open: f, a, b, e, d, c, dp

  // Notes on the sheet:
  //   By Diogo Viana & Gabriel Morgado
endmodule

module My_Adder (
  input  A,
  input  B,
  input  Cin,
  output S,
  output Cout
);

  wire and_1_out, and_2_out, xor_1_out;

  xor xor_1 (xor_1_out, A, B);
  and and_1 (and_1_out, A, B);
  and and_2 (and_2_out, xor_1_out, Cin);
  xor xor_2 (S, xor_1_out, Cin);
  xor xor_3 (Cout, and_2_out, and_1_out);
endmodule

module _4bit_Adder (
  input  [3:0] A0__A3,
  input  [3:0] B0___B3,
  input  Cout,
  output [3:0] S0___S3,
  output minus_1Cout,
  output Cout_2
);

  wire my_adder_1_cout, my_adder_2_cout;

  My_Adder my_adder_1 (.A(A0__A3[0]), .B(B0___B3[0]), .Cin(Cout), .S(S0___S3[0]), .Cout(my_adder_1_cout));
  My_Adder my_adder_2 (.A(A0__A3[1]), .B(B0___B3[1]), .Cin(my_adder_1_cout), .S(S0___S3[1]), .Cout(my_adder_2_cout));
  My_Adder my_adder_3 (.A(A0__A3[2]), .B(B0___B3[2]), .Cin(my_adder_2_cout), .S(S0___S3[2]), .Cout(minus_1Cout));
  My_Adder my_adder_4 (.A(A0__A3[3]), .B(B0___B3[3]), .Cin(minus_1Cout), .S(S0___S3[3]), .Cout(Cout_2));
endmodule

module _4bit_Adder_2 (
  input  [3:0] A3___A0,
  input  [3:0] B3___B0,
  input  Negate_B,
  output [3:0] S3___S0,
  output Zero,
  output Error,
  output Error_2
);

  wire n4bit_adder_1_minus_1cout, nor_1_out, not_1_out, not_2_out;
  wire [3:0] xor_1_out;

  assign xor_1_out = B3___B0 ^ {4{Negate_B}};  // XOR_Gate xor_1, 4 bits wide
  _4bit_Adder u_4bit_adder_1 (
    .A0__A3(A3___A0), .B0___B3(xor_1_out), .Cout(Negate_B), .S0___S3(S3___S0), .Cout_2(Error_2),
    .minus_1Cout(n4bit_adder_1_minus_1cout));
  nor nor_1 (nor_1_out, S3___S0[0], S3___S0[1], S3___S0[2], S3___S0[3]);
  xor xor_2 (Error, n4bit_adder_1_minus_1cout, Error_2);
  not not_1 (not_1_out, Error);
  not not_2 (not_2_out, Error_2);
  and and_1 (Zero, nor_1_out, not_1_out, not_2_out);
endmodule

module Decrement_4bit_Adder (
  input  [3:0] A3___A0,
  output [3:0] S3___S0,
  output Zero,
  output Error
);

  wire n4bit_adder_1_cout_2, n4bit_adder_1_minus_1cout, nor_1_out, not_1_out;

  _4bit_Adder u_4bit_adder_1 (
    .A0__A3(A3___A0), .B0___B3(4'b1110), .Cout(1'b1), .S0___S3(S3___S0), .Cout_2(n4bit_adder_1_cout_2),
    .minus_1Cout(n4bit_adder_1_minus_1cout));
  xor xor_1 (Error, n4bit_adder_1_minus_1cout, n4bit_adder_1_cout_2);
  not not_1 (not_1_out, Error);
  nor nor_1 (nor_1_out, S3___S0[0], S3___S0[1], S3___S0[2], S3___S0[3]);
  and and_1 (Zero, nor_1_out, not_1_out);
endmodule

module Increment_4bit_Adder (
  input  [3:0] A3___A0,
  output [3:0] S3___S0,
  output Zero,
  output Error
);

  wire n4bit_adder_1_cout_2, n4bit_adder_1_minus_1cout, nor_1_out, not_1_out;

  _4bit_Adder u_4bit_adder_1 (
    .A0__A3(A3___A0), .B0___B3(4'b0001), .Cout(1'b0), .S0___S3(S3___S0), .Cout_2(n4bit_adder_1_cout_2),
    .minus_1Cout(n4bit_adder_1_minus_1cout));
  xor xor_1 (Error, n4bit_adder_1_minus_1cout, n4bit_adder_1_cout_2);
  not not_1 (not_1_out, Error);
  nor nor_1 (nor_1_out, S3___S0[0], S3___S0[1], S3___S0[2], S3___S0[3]);
  and and_1 (Zero, nor_1_out, not_1_out);
endmodule

module _4bit_AND (
  input  [3:0] A3___A0,
  input  [3:0] B3___B0,
  output [3:0] S3___S0
);

  assign S3___S0 = A3___A0 & B3___B0;  // AND_Gate and_1, 4 bits wide
endmodule

module _4bit_OR (
  input  [3:0] A3___A0,
  input  [3:0] B3___B0,
  output [3:0] S3___S0
);

  assign S3___S0 = A3___A0 | B3___B0;  // OR_Gate or_1, 4 bits wide
endmodule

module _4bit_NOT (
  input  [3:0] A3___A0,
  output [3:0] S3___S0
);

  assign S3___S0 = ~A3___A0;  // NOT_Gate not_1, 4 bits wide
endmodule

module ULA (
  input  [3:0] A3___A0,
  input  [3:0] B3___B0,
  input  [2:0] S2___S0,
  output OF,
  output ZF,
  output [3:0] Y3___Y0
);

  wire decrement_4bit_adder_1_error, decrement_4bit_adder_1_zero, increment_4bit_adder_1_error,
       increment_4bit_adder_1_zero, n4bit_adder_1_error, n4bit_adder_1_zero, n4bit_adder_2_error,
       n4bit_adder_2_zero, nor_1_out, nor_2_out, nor_3_out, nor_4_out;
  wire [3:0] decrement_4bit_adder_1_s3___s0, increment_4bit_adder_1_s3___s0, n4bit_adder_1_s3___s0,
       n4bit_adder_2_s3___s0, n4bit_and_1_s3___s0, n4bit_not_1_s3___s0, n4bit_or_1_s3___s0;

  nor nor_1 (nor_1_out, A3___A0[3], A3___A0[2], A3___A0[1], A3___A0[0]);
  Decrement_4bit_Adder decrement_4bit_adder_1 (
    .A3___A0(A3___A0), .S3___S0(decrement_4bit_adder_1_s3___s0), .Zero(decrement_4bit_adder_1_zero),
    .Error(decrement_4bit_adder_1_error));
  Increment_4bit_Adder increment_4bit_adder_1 (
    .A3___A0(A3___A0), .Zero(increment_4bit_adder_1_zero), .Error(increment_4bit_adder_1_error),
    .S3___S0(increment_4bit_adder_1_s3___s0));
  Multiplexer #(.select(3), .width(4), .enable("false")) multiplexer_1 (
    .in0(A3___A0), .in1(decrement_4bit_adder_1_s3___s0), .in2(increment_4bit_adder_1_s3___s0),
    .in3(n4bit_adder_1_s3___s0), .in4(n4bit_adder_2_s3___s0), .in5(n4bit_not_1_s3___s0),
    .in6(n4bit_or_1_s3___s0), .in7(n4bit_and_1_s3___s0), .out(Y3___Y0), .sel(S2___S0));
  _4bit_Adder_2 u_4bit_adder_1 (
    .A3___A0(A3___A0), .B3___B0(B3___B0), .Negate_B(1'b0), .S3___S0(n4bit_adder_1_s3___s0),
    .Zero(n4bit_adder_1_zero), .Error(n4bit_adder_1_error));  // open: Error_2
  Multiplexer #(.select(3), .disabled(0), .enable("false")) multiplexer_2 (
    .in0(1'b0), .in1(decrement_4bit_adder_1_error), .in2(increment_4bit_adder_1_error),
    .in3(n4bit_adder_1_error), .in4(n4bit_adder_2_error), .in5(1'b0), .in6(1'b0), .in7(1'b0), .out(OF),
    .sel(S2___S0));
  Multiplexer #(.select(3), .disabled(0), .enable("false")) multiplexer_3 (
    .in0(nor_1_out), .in1(decrement_4bit_adder_1_zero), .in2(increment_4bit_adder_1_zero),
    .in3(n4bit_adder_1_zero), .in4(n4bit_adder_2_zero), .in5(nor_2_out), .in6(nor_3_out), .in7(nor_4_out),
    .out(ZF), .sel(S2___S0));
  _4bit_Adder_2 u_4bit_adder_2 (
    .A3___A0(A3___A0), .B3___B0(B3___B0), .Negate_B(1'b1), .S3___S0(n4bit_adder_2_s3___s0),
    .Zero(n4bit_adder_2_zero), .Error(n4bit_adder_2_error));  // open: Error_2
  _4bit_NOT u_4bit_not_1 (.A3___A0(A3___A0), .S3___S0(n4bit_not_1_s3___s0));
  _4bit_OR u_4bit_or_1 (.A3___A0(A3___A0), .B3___B0(B3___B0), .S3___S0(n4bit_or_1_s3___s0));
  _4bit_AND u_4bit_and_1 (.A3___A0(A3___A0), .B3___B0(B3___B0), .S3___S0(n4bit_and_1_s3___s0));
  nor nor_2 (nor_2_out, n4bit_not_1_s3___s0[3], n4bit_not_1_s3___s0[2], n4bit_not_1_s3___s0[1], n4bit_not_1_s3___s0[0]);
  nor nor_3 (nor_3_out, n4bit_or_1_s3___s0[3], n4bit_or_1_s3___s0[2], n4bit_or_1_s3___s0[1], n4bit_or_1_s3___s0[0]);
  nor nor_4 (nor_4_out, n4bit_and_1_s3___s0[3], n4bit_and_1_s3___s0[2], n4bit_and_1_s3___s0[1], n4bit_and_1_s3___s0[0]);
endmodule

module _4bit_Display (
  input  [3:0] in_1,
  output a,
  output b,
  output c,
  output d,
  output e,
  output f,
  output g,
  output Cout
);

  wire and_1_out, and_2_out, and_3_out, and_4_out, and_5_out, and_6_out, and_7_out, and_8_out, and_9_out,
       and_10_out, and_11_out, and_12_out, and_13_out, and_14_out, and_15_out, and_16_out, and_17_out,
       and_18_out, and_19_out, and_20_out, and_21_out, and_22_out, and_23_out, and_24_out, and_25_out,
       and_26_out, and_27_out, and_28_out, and_29_out, and_30_out, and_31_out, and_32_out, not_1_out;

  and and_1 (and_1_out, ~in_1[2], ~in_1[0]);  // AND_Gate
  and and_2 (and_2_out, ~in_1[3], in_1[1]);  // AND_Gate
  and and_3 (and_3_out, in_1[2], in_1[0]);
  and and_4 (and_4_out, in_1[3], ~in_1[1]);  // AND_Gate
  not not_1 (not_1_out, in_1[2]);
  and and_5 (and_5_out, ~in_1[1], ~in_1[0]);  // AND_Gate
  and and_6 (and_6_out, ~in_1[3], in_1[1], in_1[0]);  // AND_Gate
  and and_7 (and_7_out, in_1[3], ~in_1[1]);  // AND_Gate
  and and_8 (and_8_out, in_1[3], ~in_1[0]);  // AND_Gate
  and and_9 (and_9_out, ~in_1[3], ~in_1[1]);  // AND_Gate
  and and_10 (and_10_out, in_1[2], in_1[1]);
  and and_11 (and_11_out, in_1[3], ~in_1[2]);  // AND_Gate
  and and_12 (and_12_out, ~in_1[2], ~in_1[0]);  // AND_Gate
  and and_13 (and_13_out, ~in_1[3], ~in_1[2], in_1[1]);  // AND_Gate
  and and_14 (and_14_out, in_1[2], ~in_1[1], in_1[0]);  // AND_Gate
  and and_15 (and_15_out, ~in_1[3], in_1[1], ~in_1[0]);  // AND_Gate
  and and_16 (and_16_out, in_1[3], ~in_1[1]);  // AND_Gate
  and and_17 (and_17_out, in_1[3], in_1[2], in_1[0]);
  and and_18 (and_18_out, ~in_1[2], ~in_1[0]);  // AND_Gate
  and and_19 (and_19_out, ~in_1[3], in_1[1], ~in_1[0]);  // AND_Gate
  and and_20 (and_20_out, in_1[3], ~in_1[1], ~in_1[0]);  // AND_Gate
  and and_21 (and_21_out, ~in_1[3], in_1[2]);  // AND_Gate
  and and_22 (and_22_out, in_1[3], ~in_1[2], ~in_1[1]);  // AND_Gate
  and and_23 (and_23_out, in_1[2], in_1[1]);
  and and_24 (and_24_out, ~in_1[3], ~in_1[1], ~in_1[0]);  // AND_Gate
  and and_25 (and_25_out, in_1[3], ~in_1[2], ~in_1[0]);  // AND_Gate
  and and_26 (and_26_out, ~in_1[3], ~in_1[2], in_1[1]);  // AND_Gate
  and and_27 (and_27_out, in_1[2], ~in_1[1]);  // AND_Gate
  and and_28 (and_28_out, in_1[3], ~in_1[1]);  // AND_Gate
  and and_29 (and_29_out, in_1[3], in_1[2]);
  and and_30 (and_30_out, ~in_1[3], in_1[1], ~in_1[0]);  // AND_Gate
  and and_31 (and_31_out, in_1[3], in_1[2]);
  and and_32 (and_32_out, in_1[3], in_1[1]);
  or or_1 (a, and_1_out, and_2_out, and_3_out, and_4_out);
  or or_2 (b, not_1_out, and_5_out, and_6_out, and_7_out, and_8_out);
  or or_3 (c, in_1[0], and_9_out, and_10_out, and_11_out);
  or or_4 (d, and_12_out, and_13_out, and_14_out, and_15_out, and_16_out, and_17_out);
  or or_5 (e, and_18_out, and_19_out, and_20_out);
  or or_6 (f, and_21_out, and_22_out, and_23_out, and_24_out, and_25_out);
  or or_7 (g, and_26_out, and_27_out, and_28_out, and_29_out, and_30_out);
  or or_8 (Cout, and_31_out, and_32_out);
endmodule

module _4bit_Negative_Display (
  input  [3:0] in_1,
  output a,
  output b,
  output c,
  output d,
  output e,
  output f,
  output g,
  output Cout
);

  wire and_1_out, and_2_out, and_3_out, and_4_out, and_5_out, and_6_out, and_7_out, and_8_out, and_9_out,
       and_10_out, and_11_out, and_12_out, and_13_out, and_14_out, and_15_out, and_16_out, and_17_out,
       and_18_out, and_19_out, and_20_out, and_21_out, and_22_out, and_23_out, and_24_out, and_25_out,
       not_1_out;

  and and_1 (and_1_out, ~in_1[2], ~in_1[0]);  // AND_Gate
  and and_2 (and_2_out, in_1[1], ~in_1[0]);  // AND_Gate
  and and_3 (and_3_out, ~in_1[3], in_1[1]);  // AND_Gate
  and and_4 (and_4_out, in_1[2], ~in_1[1], in_1[0]);  // AND_Gate
  and and_5 (and_5_out, in_1[3], ~in_1[2]);  // AND_Gate
  and and_6 (and_6_out, ~in_1[3], ~in_1[2]);  // AND_Gate
  and and_7 (and_7_out, ~in_1[1], ~in_1[0]);  // AND_Gate
  and and_8 (and_8_out, in_1[3], in_1[2]);
  and and_9 (and_9_out, ~in_1[3], in_1[1], in_1[0]);  // AND_Gate
  and and_10 (and_10_out, ~in_1[2], ~in_1[1]);  // AND_Gate
  not not_1 (not_1_out, in_1[1]);
  and and_11 (and_11_out, ~in_1[3], in_1[2]);  // AND_Gate
  and and_12 (and_12_out, in_1[3], ~in_1[2]);  // AND_Gate
  and and_13 (and_13_out, ~in_1[2], ~in_1[0]);  // AND_Gate
  and and_14 (and_14_out, ~in_1[2], in_1[1]);  // AND_Gate
  and and_15 (and_15_out, in_1[2], ~in_1[1], in_1[0]);  // AND_Gate
  and and_16 (and_16_out, in_1[1], ~in_1[0]);  // AND_Gate
  and and_17 (and_17_out, ~in_1[2], ~in_1[0]);  // AND_Gate
  and and_18 (and_18_out, in_1[1], ~in_1[0]);  // AND_Gate
  and and_19 (and_19_out, ~in_1[1], ~in_1[0]);  // AND_Gate
  and and_20 (and_20_out, ~in_1[3], in_1[2]);  // AND_Gate
  and and_21 (and_21_out, in_1[3], ~in_1[2]);  // AND_Gate
  and and_22 (and_22_out, ~in_1[2], in_1[1]);  // AND_Gate
  and and_23 (and_23_out, in_1[2], ~in_1[1]);  // AND_Gate
  and and_24 (and_24_out, in_1[3], ~in_1[0]);  // AND_Gate
  and and_25 (and_25_out, in_1[1], ~in_1[0]);  // AND_Gate
  or or_1 (a, and_1_out, and_2_out, and_3_out, and_4_out, and_5_out);
  or or_2 (b, and_6_out, and_7_out, and_8_out, and_9_out, and_10_out);
  or or_3 (c, in_1[0], not_1_out, and_11_out, and_12_out);
  or or_4 (d, and_13_out, and_14_out, and_15_out, and_16_out);
  or or_5 (e, and_17_out, and_18_out);
  or or_6 (f, and_19_out, and_20_out, and_21_out);
  or or_7 (g, and_22_out, and_23_out, and_24_out, and_25_out);

  assign Cout = in_1[3];
endmodule

module _4bit_Display_2 (
  input  S,
  input  [3:0] in_2,
  output a,
  output b,
  output c,
  output d,
  output e,
  output f,
  output g,
  output Cout,
  output Mout
);

  wire multiplexer_1_out, n4bit_display_1_a, n4bit_display_1_b, n4bit_display_1_c, n4bit_display_1_cout,
       n4bit_display_1_d, n4bit_display_1_e, n4bit_display_1_f, n4bit_display_1_g,
       n4bit_negative_display_1_a, n4bit_negative_display_1_b, n4bit_negative_display_1_c,
       n4bit_negative_display_1_cout, n4bit_negative_display_1_d, n4bit_negative_display_1_e,
       n4bit_negative_display_1_f, n4bit_negative_display_1_g;

  _4bit_Display u_4bit_display_1 (
    .in_1(in_2), .a(n4bit_display_1_a), .b(n4bit_display_1_b), .c(n4bit_display_1_c), .d(n4bit_display_1_d),
    .e(n4bit_display_1_e), .f(n4bit_display_1_f), .g(n4bit_display_1_g), .Cout(n4bit_display_1_cout));
  _4bit_Negative_Display u_4bit_negative_display_1 (
    .in_1(in_2), .a(n4bit_negative_display_1_a), .b(n4bit_negative_display_1_b),
    .c(n4bit_negative_display_1_c), .d(n4bit_negative_display_1_d), .e(n4bit_negative_display_1_e),
    .f(n4bit_negative_display_1_f), .g(n4bit_negative_display_1_g), .Cout(n4bit_negative_display_1_cout));
  Multiplexer #(.enable("false")) multiplexer_1 (
    .in0(n4bit_display_1_cout), .in1(n4bit_negative_display_1_cout), .out(multiplexer_1_out), .sel(S));
  Demultiplexer #(.enable("false")) demultiplexer_1 (.out0(Cout), .out1(Mout), .in(multiplexer_1_out), .sel(S));
  Multiplexer #(.enable("false")) multiplexer_2 (
    .in0(n4bit_display_1_a), .in1(n4bit_negative_display_1_a), .out(a), .sel(S));
  Multiplexer #(.enable("false")) multiplexer_3 (
    .in0(n4bit_display_1_b), .in1(n4bit_negative_display_1_b), .out(b), .sel(S));
  Multiplexer #(.enable("false")) multiplexer_4 (
    .in0(n4bit_display_1_c), .in1(n4bit_negative_display_1_c), .out(c), .sel(S));
  Multiplexer #(.enable("false")) multiplexer_5 (
    .in0(n4bit_display_1_d), .in1(n4bit_negative_display_1_d), .out(d), .sel(S));
  Multiplexer #(.enable("false")) multiplexer_6 (
    .in0(n4bit_display_1_e), .in1(n4bit_negative_display_1_e), .out(e), .sel(S));
  Multiplexer #(.enable("false")) multiplexer_7 (
    .in0(n4bit_display_1_f), .in1(n4bit_negative_display_1_f), .out(f), .sel(S));
  Multiplexer #(.enable("false")) multiplexer_8 (
    .in0(n4bit_display_1_g), .in1(n4bit_negative_display_1_g), .out(g), .sel(S));
endmodule
