// Logisim project circuito_trabalho.circ as structural Verilog: 1 circuit, main circuit main
module main (
);

  wire and_1_out, and_2_out, and_3_out, and_4_out, and_5_out, and_6_out, clock_1_out, j_k_ff_1_qn,
       j_k_ff_2_qn, j_k_ff_3_qn, j_k_ff_4_qn, or_1_out, or_2_out, or_3_out, or_4_out, or_5_out;
  wire [3:0] j_k_ff_1_q;

  Clock clock_1 (.out(clock_1_out));
  Hex_Digit_Display hex_digit_display_1 (.value(j_k_ff_1_q));  // open: dp
  or or_1 (or_1_out, and_2_out, and_1_out);
  and and_1 (and_1_out, j_k_ff_1_q[3], j_k_ff_1_q[1]);
  and and_2 (and_2_out, j_k_ff_4_qn, j_k_ff_3_qn);
  J_K_Flip_Flop j_k_ff_1 (
    .J(j_k_ff_1_q[1]), .clk(clock_1_out), .K(or_1_out), .Q(j_k_ff_1_q[0]), .Qn(j_k_ff_1_qn));  // open: preset, en, reset
  or or_2 (or_2_out, j_k_ff_1_q[2], and_3_out);
  and and_3 (and_3_out, j_k_ff_1_q[0], j_k_ff_4_qn);
  J_K_Flip_Flop j_k_ff_2 (
    .J(1'b1), .clk(clock_1_out), .K(or_2_out), .Q(j_k_ff_1_q[1]), .Qn(j_k_ff_2_qn));  // open: preset, en, reset
  and and_4 (and_4_out, j_k_ff_1_q[0], j_k_ff_1_q[1]);
  or or_3 (or_3_out, j_k_ff_1_q[3], and_4_out);
  or or_4 (or_4_out, j_k_ff_1_q[3], j_k_ff_1_q[0]);
  J_K_Flip_Flop j_k_ff_3 (
    .J(or_3_out), .clk(clock_1_out), .K(or_4_out), .Q(j_k_ff_1_q[2]), .Qn(j_k_ff_3_qn));  // open: preset, en, reset
  and and_5 (and_5_out, j_k_ff_1_qn, j_k_ff_2_qn);
  and and_6 (and_6_out, j_k_ff_3_qn, j_k_ff_1_qn);
  or or_5 (or_5_out, and_5_out, and_6_out);
  J_K_Flip_Flop j_k_ff_4 (
    .J(or_5_out), .clk(clock_1_out), .K(j_k_ff_1_q[0]), .Q(j_k_ff_1_q[3]), .Qn(j_k_ff_4_qn));  // open: preset, en, reset
endmodule
